# Fritzing sketch piano (saved by Fritzing 0.8.7b)
breadboards: 1

parts:
  Часть1 = Arduino Uno (Rev3)
  S1 = Pushbutton [package="[THT]"]
  S2 = Pushbutton [package="[THT]"]
  S3 = Pushbutton [package="[THT]"]
  J1 = Piezo Speaker  # not connected
  R1 = Resistor [tolerance=±5% resistance=220 package=THT]
  R2 = Resistor [tolerance=±5% resistance=220 package=THT]
  R3 = Resistor [tolerance=±5% resistance=220 package=THT]

nets:
  N1: Часть1.D8, S2.Pin_3, S2.Pin_4, R2.Pin_1
  N2: Часть1.D9_PWM, S1.Pin_3, S1.Pin_4, R1.Pin_0
  N3: Часть1.D7, Часть1.5V, S1.Pin_1, S1.Pin_2, S2.Pin_1, S2.Pin_2, S3.Pin_1, S3.Pin_2, S3.Pin_3, S3.Pin_4, R1.Pin_1, R2.Pin_0, R3.Pin_0, R3.Pin_1
